# Fritzing sketch ble-alert (saved by Fritzing 0.9.3b)
breadboards: 1

parts:
  Part1 = Arduino Nano (Rev3.0)
  Part2 = HM-10
  Raspberry_Pi_1 = Raspberry Pi 3 [part_number=RPI-3-V1.2]  # not connected
  Raspberry_Pi_Zero1 = Raspberry Pi Zero  # not connected

nets:
  N1: Part1.GND, Part2.connector14
  N2: Part1.5V, Part2.connector16
  N3: Part1.A5, Part2.connector12
  N4: Part1.A4, Part2.connector13
